# Fritzing sketch IoT-2 (saved by Fritzing 0.9.9b)
breadboards: 1

parts:
  J1 = Piezo Speaker
  LCD2 = LCD screen
  LCM1602_IIC2 = LCM1602 IIC [part_number="LCM1602 IIC" chip_label="LCM1602 IIC" package="DIP (Dual Inline) [THT]"]
  PIR1 = PIR sensor
  PIR2 = PIR sensor
  U2 = NodeMCU V1.0
  LED1 = LED - 5mm [color="Red (633nm)" current=0.030 package="5 mm [THT]"]
  LED2 = LED - 5mm [color="Red (633nm)" current=0.030 package="5 mm [THT]"]
  LED3 = LED - 5mm [color="Red (633nm)" current=0.030 package="5 mm [THT]"]
  LED4 = LED - 5mm [color="Red (633nm)" current=0.030 package="5 mm [THT]"]

nets:
  GND: J1.pin1, LCM1602_IIC2.GND, PIR1.GND, PIR2.GND, U2.GND, LED1.cathode, LED2.cathode, LED3.cathode, LED4.cathode
  N1: J1.pin2, U2.D6
  VSS: LCD2.VSS, LCM1602_IIC2.VSS
  VDD: LCD2.VDD, LCM1602_IIC2.VDD
  N2: LCD2.V0, LCM1602_IIC2.V0
  N3: LCD2.RS, LCM1602_IIC2.RS
  N4: LCD2.R/W, LCM1602_IIC2.RW
  N5: LCD2.E, LCM1602_IIC2.E
  N6: LCD2.DB0, LCM1602_IIC2.D0
  N7: LCD2.DB1, LCM1602_IIC2.D1
  N8: LCD2.DB2, LCM1602_IIC2.D2
  N9: LCD2.DB3, LCM1602_IIC2.D3
  N10: LCD2.DB4, LCM1602_IIC2.D4
  N11: LCD2.DB5, LCM1602_IIC2.D5
  N12: LCD2.DB6, LCM1602_IIC2.D6
  N13: LCD2.DB7, LCM1602_IIC2.D7
  N14: LCD2.LED+, LCM1602_IIC2.A
  N15: LCD2.LED-, LCM1602_IIC2.K
  VDD_2: LCM1602_IIC2.VCC, PIR1.VDD, PIR2.VDD, U2.3V3
  N16: LCM1602_IIC2.SDA, U2.D2
  N17: LCM1602_IIC2.SCL, U2.D1
  N18: LCM1602_IIC2.LED_A, LCM1602_IIC2.LED_B
  N19: PIR1.SIG, U2.D4
  N20: PIR2.SIG, U2.D3
  N21: U2.D0, LED3.anode
  N22: U2.D5, LED4.anode
  N23: U2.D7, LED1.anode
  N24: U2.D8, LED2.anode

custom parts:
  LCM1602 IIC: I2C-Module to use a 1602 or 2004 LCD on with the wire.h libory Serial LCD Modul
  NodeMCU V1.0: ESP8266 based NodeMCU
